# Fritzing sketch Spod3Fritzing (saved by Fritzing 1.0.1rc)
breadboards: 2

parts:
  Part1 = Arduino Nano (Rev3.0) (ICSP)
  Mod1 = MQ-7 breakout
  Mod2 = MQ-7 breakout
  Mod3 = MQ-7 breakout
  Mod4 = MQ-7 breakout
  Mod5 = MQ-7 breakout
  Mod6 = MQ-7 breakout
  LLC1 = Logic Level Converter [package="Breakout board"]
  LLC2 = Logic Level Converter [package="Breakout board"]
  R1 = Resistor [tolerance=±1% resistance=10000 package="1206 [SMD]"]
  R2 = Resistor [tolerance=±1% resistance=10000 package="1206 [SMD]"]
  R3 = Resistor [tolerance=±1% resistance=10000 package="1206 [SMD]"]
  R4 = Resistor [tolerance=±1% resistance=10000 package="1206 [SMD]"]
  R5 = Resistor [tolerance=±1% resistance=10000 package="1206 [SMD]"]
  R6 = Resistor [tolerance=±1% resistance=10000 package="1206 [SMD]"]
  Part2 = Adafruit BME680

nets:
  N1: Part1.RESET, LLC1.H-GND, LLC2.H-GND, Part2.GND
  GND: Part1.GND, Mod1.GND, Mod2.GND, Mod3.GND, Mod4.GND, Mod5.GND, Mod6.GND, LLC1.L-GND, LLC2.L-GND, R1.Pin_0, R2.Pin_0, R3.Pin_0, R4.Pin_0, R5.Pin_0, R6.Pin_0
  N2: Part1.D11/MOSI, Part2.SDI/SDA
  N3: Part1.D12/MISO, Part2.SCK/SCL
  VCC: Part1.A7, Mod1.VCC, Mod2.VCC, Mod3.VCC, Mod4.VCC, Mod5.VCC, Mod6.VCC, LLC1.LV, LLC2.LV
  N4: Part1.A5, LLC2.HV3
  N5: Part1.A4, LLC2.HV4
  N6: Part1.A3, LLC1.HV1
  N7: Part1.A2, LLC1.HV2
  N8: Part1.A1, LLC1.HV3
  N9: Part1.A0, LLC1.HV4
  3V3: Part1.3V3, LLC1.HV, LLC2.HV, Part2.VIN
  N10: Mod1.AO, LLC1.LV4, R1.Pin_1
  N11: Mod2.AO, LLC1.LV3, R2.Pin_1
  N12: Mod3.AO, LLC1.LV2, R3.Pin_1
  N13: Mod4.AO, LLC1.LV1, R4.Pin_1
  N14: Mod5.AO, LLC2.LV4, R5.Pin_1
  N15: Mod6.AO, LLC2.LV3, R6.Pin_1

custom parts:
  MQ-7 breakout: MQ-5 gas sensor
  Logic Level Converter: 5V to/from 3.3V logic level converter
